# Fritzing sketch CapteurQUV (saved by Fritzing 0.9.3b)
circuit board: 7.41409cm x 6.42003cm
breadboards: 1

parts:
  NodeMCU = IC, DIP package, 30 pins [chip_label=NodeMCU]
  5V = npn-Powertransistor [package="TO220 [THT]"]
  hc-sr1 = hc-sr04
  R1_1K = Resistor [tolerance=±5% resistance=1k package=THT]
  R2_1K = Resistor [tolerance=±5% resistance=1k package=THT]
  R3_1K = Resistor [tolerance=±5% resistance=1k package=THT]
  VCC1 = Battery block 9V
  DHT22 = Basic FET P-Channel [package="TO220 [THT]"]
  J1 = Basic Flex Resistor
  J2 = Basic Flex Resistor
  Q1 = Basic FET P-Channel [package="TO220 [THT]"]
  R1 = Resistor [tolerance=±5% resistance=220 package=THT]

nets:
  N1: NodeMCU.pin1, DHT22.drain
  N2: NodeMCU.pin2, DHT22.gate
  N3: NodeMCU.pin8, Q1.gate, R1.Pin_0
  N4: NodeMCU.pin9, R3_1K.Pin_0, Q1.source, R1.Pin_1
  N5: NodeMCU.pin11, DHT22.source
  N6: NodeMCU.pin13, R1_1K.Pin_0, R2_1K.Pin_1
  N7: NodeMCU.pin14, hc-sr1.Trig
  N8: NodeMCU.pin15, J1.Pin_2
  N9: NodeMCU.pin25, 5V.collector, VCC1.-
  N10: NodeMCU.pin28, J1.pin_1
  N11: NodeMCU.pin30, 5V.emitter, hc-sr1.VCC
  N12: 5V.base, J2.pin_1
  N13: hc-sr1.Echo, R1_1K.Pin_1
  N14: hc-sr1.GND, Q1.drain
  N15: R2_1K.Pin_0, R3_1K.Pin_1
  N16: VCC1.+, J2.Pin_2
