# Fritzing sketch CapteurQUV_2.0 (saved by Fritzing 0.9.3b)
circuit board: 7cm x 5cm
breadboards: 1

parts:
  Cable = female pin header, 6 pins [form="♀ (female)"]
  Oled = OLED 0.96" 128x64 I2C SSD1306
  Bouton = mystery part, 6 pins [chip_label=?]
  NodeMCU = NodeMCU V1.0

nets:
  N1: Cable.pin2, NodeMCU.Vin
  VCC: Cable.pin3, Oled.VCC, NodeMCU.3V3
  N2: Cable.pin4, NodeMCU.D8
  N3: Cable.pin5, NodeMCU.D7
  N4: Cable.pin6, NodeMCU.D6
  GND: Oled.GND, Bouton.pin3, NodeMCU.GND
  N5: Oled.SCL, NodeMCU.D1
  N6: Oled.SCA, NodeMCU.D2
  N7: Bouton.pin6, NodeMCU.D3

custom parts:
  NodeMCU V1.0: ESP8266 based NodeMCU
