# Fritzing sketch CapteurQUV_2.1 (saved by Fritzing 0.9.3b)
circuit board: 6.87823cm x 8.94362cm
breadboards: 1

parts:
  Oled = OLED 0.96" 128x64 I2C SSD1306
  Bouton = mystery part, 6 pins [chip_label=?]
  NodeMCU = NodeMCU V1.0
  Cable1 = double row female pin header, 6 pins [form="♀ (female)"]
  Cable2 = double row female pin header, 6 pins [form="♀ (female)"]
  HC-SR04 = female pin header, 4 pins [form="♀ (female)"]
  DHT22 = female pin header, 3 pins [form="♀ (female)"]

nets:
  VCC: Oled.VCC, NodeMCU.3V3, Cable1.pin3
  GND: Oled.GND, Bouton.pin3, NodeMCU.GND, Cable1.pin2
  N1: Oled.SCL, NodeMCU.D1
  N2: Oled.SCA, NodeMCU.D2
  N3: NodeMCU.D5, Cable1.pin4
  N4: NodeMCU.D6, Cable1.pin5
  N5: NodeMCU.D7, Cable1.pin6
  N6: NodeMCU.Vin, Cable1.pin1
  N7: Cable2.pin1, HC-SR04.pin2
  N8: Cable2.pin2, HC-SR04.pin3
  N9: Cable2.pin3, DHT22.pin3
  N10: Cable2.pin4, DHT22.pin2
  N11: Cable2.pin5, HC-SR04.pin4, DHT22.pin1
  N12: Cable2.pin6, HC-SR04.pin1

custom parts:
  NodeMCU V1.0: ESP8266 based NodeMCU
